# Fritzing sketch receiver (saved by Fritzing 0.9.3b)
breadboards: 1

parts:
  UNO_main = Arduino Uno (Rev3)
  rf = NRF24L01+ Breakout Board

nets:
  N1: UNO_main.D9_PWM, rf.CE
  N2: UNO_main.D10_PWM/SS, rf.CS
  N3: UNO_main.D11_PWM/MOSI, rf.MOSI
  N4: UNO_main.D12/MISO, rf.MISO
  N5: UNO_main.D13/SCK, rf.SCK
  GND: UNO_main.GND, rf.GND
  1: UNO_main.D2
  2: UNO_main.D3_PWM
  3V3: UNO_main.3V3, rf.VCC
