# Fritzing sketch transmitter (saved by Fritzing 0.9.3b)
breadboards: 1

parts:
  Arduino_(main) = Arduino Uno (Rev3)
  rf1 = NRF24L01+ Breakout Board

nets:
  N1: Arduino_(main).D9_PWM, rf1.CE
  N2: Arduino_(main).D10_PWM/SS, rf1.CS
  N3: Arduino_(main).D11_PWM/MOSI, rf1.MOSI
  N4: Arduino_(main).D12/MISO, rf1.MISO
  N5: Arduino_(main).D13/SCK, rf1.SCK
  GND: Arduino_(main).GND, rf1.GND
  3V3: Arduino_(main).3V3, rf1.VCC
